# Fritzing sketch Electronics box (saved by Fritzing 0.9.3b)
breadboards: 1

parts:
  Stepper_driver = IC, DIP package, 16 pins [chip_label="Polulu md20b"]
  Stepper_driver_2 = IC, DIP package, 16 pins [chip_label="Polulu md20b"]
  R1 = Resistor [tolerance=±5% resistance=330 package=THT]
  R2 = Resistor [tolerance=±5% resistance=330 package=THT]
  Fathom-X_Tether_Interface_Board = IC, DIP package, 4 pins [chip_label="\nFathom-X Tether Interface Board"]
  S1 = Pushbutton [package=THT]
  S3 = Pushbutton [package=THT]
  Camera_servo = Basic Servo
  LED_lights = IC, SIP package, 3 pins [chip_label="Lumen subsea light"]
  Teensy1 = Teensy 4.0
  Teensy2 = Teensy 4.0
  Raspberry_Pi_4 = Raspberry Pi 2
  Pressure_sensor1 = IC, DIP package, 4 pins [chip_label=MS5837-30BA1]
  Adafruit_9dof_IMU1 = IC, DIP package, 4 pins [chip_label=IMU]
  Echo_sounder1 = IC, DIP package, 4 pins [chip_label=PING-SONAR]
  Leak_sensor = IC, DIP package, 4 pins [chip_label="SOS Leak Sensor"]
  Stepper_motor_1 = Stepper Motor - Bipolar
  Stepper_motor_2 = Stepper Motor - Bipolar
  U2 = Mini-360 DC-DC Buck converter [package=THT]
  U3 = Mini-360 DC-DC Buck converter [package=THT]
  C2 = Electrolytic Capacitor [capacitance=1000µF voltage=50V package="300 mil [THT, electrolytic]"]
  C1 = Electrolytic Capacitor [capacitance=1000µF voltage=50V package="300 mil [THT, electrolytic]"]
  X1 = Header 8 [package=1x08_smd_alt]
  part = Header 8 [package=1x08_smd_alt]
  X2 = Header 8 [package=1x08_smd_alt]
  part_2 = Header 8 [package=1x08_smd_alt]
  X3 = Header 10 [package=1x10-2mm-smd]  # not connected
  part_3 = Header 10 [package=1x10-2mm-smd]  # not connected
  X4 = Header 10 [package=1x10-2mm-smd]  # not connected
  part_4 = Header 10 [package=1x10-2mm-smd]  # not connected

nets:
  5V custom PCB: Stepper_driver.pin5, Stepper_driver.pin6, Stepper_driver_2.pin5, Stepper_driver_2.pin6, S1.leg1, S3.leg1
  N1: Stepper_driver.pin7, Teensy1.pin_8
  N2: Stepper_driver.pin8, Teensy1.pin_7
  GND(5V): Stepper_driver.pin9, Stepper_driver_2.pin9
  N3: Stepper_driver.pin11, part_2.5
  N4: Stepper_driver.pin12, part_2.6
  N5: Stepper_driver.pin13, part_2.7
  N6: Stepper_driver.pin14, part_2.8
  GND(12V) custom PCB: Stepper_driver.pin15, Stepper_driver_2.pin15
  12V custom PCB: Stepper_driver.pin16, Stepper_driver_2.pin16
  N7: Stepper_driver_2.pin7, Teensy1.pin_5
  N8: Stepper_driver_2.pin8, Teensy1.pin_4
  N9: Stepper_driver_2.pin11, part_2.1
  N10: Stepper_driver_2.pin12, part_2.2
  N11: Stepper_driver_2.pin13, part_2.3
  N12: Stepper_driver_2.pin14, part_2.4
  N13: R1.Pin_0, S1.leg0, Teensy1.pin_9
  GND: R1.Pin_1, R2.Pin_1, Fathom-X_Tether_Interface_Board.pin3, Pressure_sensor1.pin3, Adafruit_9dof_IMU1.pin3, Echo_sounder1.pin2, Leak_sensor.pin2, U2.OUT-, U3.IN-, U3.OUT-, C2.-, C1.-, X1.6, X1.8
  N14: R2.Pin_0, S3.leg0, Teensy1.pin_6
  N15: Fathom-X_Tether_Interface_Board.pin1, part.3
  N16: Fathom-X_Tether_Interface_Board.pin2, part.4
  12V: Fathom-X_Tether_Interface_Board.pin4
  GND(5V) Custom PCB: Camera_servo.gnd, Teensy1.pin_17, Teensy1.pin_32, Teensy2.pin_17, Teensy2.pin_32, Raspberry_Pi_4.GND
  5V: Camera_servo.vcc, Teensy1.pin33, Teensy2.pin33, Raspberry_Pi_4.5V, Pressure_sensor1.pin4, Adafruit_9dof_IMU1.pin4, Echo_sounder1.pin1
  N17: Camera_servo.pulse, Raspberry_Pi_4.GPIO16
  GND(12V) Custom PCB: LED_lights.pin1
  12V Custom PCB: LED_lights.pin2
  N18: LED_lights.pin3, Raspberry_Pi_4.GPIO20
  N19: Teensy1.pin_2, Raspberry_Pi_4.GPIO4
  N20: Teensy1.pin_3, Raspberry_Pi_4.GPIO5
  N21: Teensy2.pin_2, Raspberry_Pi_4.GPIO14
  N22: Teensy2.pin_3, Raspberry_Pi_4.GPIO15
  N23: Teensy2.pin_4, Leak_sensor.pin3
  N24: Teensy2.pin_9, Echo_sounder1.pin4
  N25: Teensy2.pin_10, Echo_sounder1.pin3
  N26: Teensy2.pin_16, Teensy2.pin_31, Leak_sensor.pin1
  N27: Teensy2.pin_25, Pressure_sensor1.pin1, Adafruit_9dof_IMU1.pin1
  N28: Teensy2.pin_26, Pressure_sensor1.pin2, Adafruit_9dof_IMU1.pin2
  N29: Stepper_motor_1.A, X2.8
  N30: Stepper_motor_1.C, X2.7
  N31: Stepper_motor_1.B, X2.6
  N32: Stepper_motor_1.D, X2.5
  N33: Stepper_motor_2.A, X2.4
  N34: Stepper_motor_2.C, X2.3
  N35: Stepper_motor_2.B, X2.2
  N36: Stepper_motor_2.D, X2.1
  N37: U2.IN-, part.2
  N38: U2.IN+, part.1
  12 V: U2.OUT+, U3.IN+, C1.+, X1.5
  5 V: U3.OUT+, C2.+, X1.7
  Theter cable (Blue, Orange, Brown): X1.1
  Theter cable (Blue/W, Orange/W, Brown/W): X1.2
  Theter cable - (Green): X1.3
  Theter cable - (Green/White): X1.4

custom parts:
  Teensy 4.0: The Teensy is a complete USB-based microcontoller development system, in a very small footprint, capable of implementing many types of projects. All programming is done via the USB port. No special programmer is needed, only a standard micro-USB cable and a PC or Macintosh with a USB port.
  Mini-360 DC-DC Buck converter: Mini-360 DC-DC Buck converter. Tiny buck step down voltage converter, input voltage 4.75 to 23V output 1 to 17V adjustable. Available from ebay and the like.
