# Fritzing sketch Electronics box7' (saved by Fritzing 0.9.3b)
breadboards: 1

parts:
  Stepper_driver = IC, DIP package, 16 pins [chip_label="Polulu md20b"]
  Stepper_driver_2 = IC, DIP package, 16 pins [chip_label="Polulu md20b"]
  R1 = Resistor [tolerance=±5% resistance=330 package=THT]
  R2 = Resistor [tolerance=±5% resistance=330 package=THT]
  Fathom-X_Tether_Interface_Board = IC, DIP package, 4 pins [chip_label="\nFathom-X Tether Interface Board"]
  S1 = Pushbutton [package=THT]
  S2 = Pushbutton [package=THT]
  Camera_servo = Basic Servo
  LED_lights = IC, SIP package, 3 pins [chip_label="Lumen subsea light"]
  Teensy1 = Teensy 4.0
  Teensy2 = Teensy 4.0
  Raspberry_Pi_4 = Raspberry Pi 2
  Leak_sensor = IC, DIP package, 4 pins [chip_label="SOS Leak Sensor"]
  Stepper_motor_1 = Stepper Motor - Bipolar
  Stepper_motor_2 = Stepper Motor - Bipolar
  U2 = Mini-360 DC-DC Buck converter [package=THT]
  U3 = Mini-360 DC-DC Buck converter [package=THT]
  C2 = Electrolytic Capacitor [capacitance=1000µF voltage=50V package="300 mil [THT, electrolytic]"]
  C1 = Electrolytic Capacitor [capacitance=1000µF voltage=50V package="300 mil [THT, electrolytic]"]
  X1 = Header 8 [package=1x08_smd_alt]
  part = Header 8 [package=1x08_smd_alt]
  X2 = Header 8 [package=1x08_smd_alt]
  part_2 = Header 8 [package=1x08_smd_alt]
  X4 = Header 10 [package=1x10-2mm-smd]
  part_3 = Header 10 [package=1x10-2mm-smd]  # not connected
  X3 = Header 10 [package=1x10-2mm-smd]
  part_4 = Header 10 [package=1x10-2mm-smd]
  Pressure_sensor2 = IC, DIP package, 4 pins [chip_label=MS5837-30BA1]
  Echo_sounder2 = IC, DIP package, 4 pins [chip_label=PING-SONAR]
  Adafruit_9dof_IMU3 = IC, DIP package, 4 pins [chip_label=IMU]
  Switch = IC, DIP package, 4 pins [chip_label="SwitchBlox Nano"]

nets:
  5V: Stepper_driver.pin5, Stepper_driver.pin6, Stepper_driver_2.pin5, Stepper_driver_2.pin6, Camera_servo.vcc, Teensy1.pin33, Teensy2.pin33, Raspberry_Pi_4.5V, Adafruit_9dof_IMU3.pin4
  N1: Stepper_driver.pin7, Teensy1.pin_8
  N2: Stepper_driver.pin8, Teensy1.pin_7
  GND(5V): Stepper_driver.pin9, Stepper_driver_2.pin9, R1.Pin_1, R2.Pin_1, Camera_servo.gnd, Teensy1.pin_17, Teensy1.pin_32, Teensy2.pin_1, Teensy2.pin_32, Raspberry_Pi_4.GND, U3.OUT-, C2.-
  N3: Stepper_driver.pin11, part_2.5
  N4: Stepper_driver.pin12, part_2.6
  N5: Stepper_driver.pin13, part_2.7
  N6: Stepper_driver.pin14, part_2.8
  GND(12V): Stepper_driver.pin15, Stepper_driver_2.pin15, Fathom-X_Tether_Interface_Board.pin3, U2.OUT-, U3.IN-, C1.-, Switch.pin2
  12V: Stepper_driver.pin16, Stepper_driver_2.pin16, Fathom-X_Tether_Interface_Board.pin4, Switch.pin1
  N7: Stepper_driver_2.pin7, Teensy1.pin_5
  N8: Stepper_driver_2.pin8, Teensy1.pin_4
  N9: Stepper_driver_2.pin11, part_2.1
  N10: Stepper_driver_2.pin12, part_2.2
  N11: Stepper_driver_2.pin13, part_2.3
  N12: Stepper_driver_2.pin14, part_2.4
  N13: R1.Pin_0, Teensy1.pin_9, part_4.10
  N14: R2.Pin_0, Teensy1.pin_6, part_4.9
  N15: Fathom-X_Tether_Interface_Board.pin1, part.3
  N16: Fathom-X_Tether_Interface_Board.pin2, part.4
  X1-5V: S1.leg0, S2.leg0, part.7, Pressure_sensor2.pin4, Echo_sounder2.pin1
  N17: S1.leg1, X3.9
  N18: S2.leg1, X3.10
  N19: Camera_servo.pulse, Raspberry_Pi_4.GPIO16
  X1-12V: LED_lights.pin1, part.5
  X1-GND(12V): LED_lights.pin2, part.6
  N20: LED_lights.pin3, part_4.8
  N21: Teensy2.pin_4, Leak_sensor.pin3
  N22: Teensy2.pin_9, part_4.2
  N23: Teensy2.pin_10, part_4.1
  N24: Teensy2.pin_16, Teensy2.pin_31, Leak_sensor.pin1
  N25: Teensy2.pin_21, X4.5
  N26: Teensy2.pin_22, X4.6
  N27: Teensy2.pin_23, X4.7
  N28: Teensy2.pin_24, X4.8
  N29: Teensy2.pin_25, part_4.4, Adafruit_9dof_IMU3.pin1
  N30: Teensy2.pin_26, part_4.3, Adafruit_9dof_IMU3.pin2
  N31: Teensy2.pin_27, X4.9
  N32: Teensy2.pin_28, X4.10
  N33: Raspberry_Pi_4.GPIO12, X3.8
  GND: Leak_sensor.pin2, X1.6, X1.8, Adafruit_9dof_IMU3.pin3
  N34: Stepper_motor_1.A, X2.8
  N35: Stepper_motor_1.C, X2.7
  N36: Stepper_motor_1.B, X2.6
  N37: Stepper_motor_1.D, X2.5
  N38: Stepper_motor_2.A, X2.4
  N39: Stepper_motor_2.C, X2.3
  N40: Stepper_motor_2.B, X2.2
  N41: Stepper_motor_2.D, X2.1
  N42: U2.IN-, part.2
  N43: U2.IN+, part.1
  12 V: U2.OUT+, U3.IN+, C1.+, X1.5
  5 V: U3.OUT+, C2.+, X1.7
  Theter cable (Blue, Orange, Brown): X1.1
  Theter cable (Blue/W, Orange/W, Brown/W): X1.2
  Theter cable - (Green): X1.3
  Theter cable - (Green/White): X1.4
  X1-GND(5V): part.8, Pressure_sensor2.pin3, Echo_sounder2.pin2
  Switch R+: X4.1
  Switch R-: X4.2
  Switch T+: X4.3
  Switch T-: X4.4
  N44: X3.1, Echo_sounder2.pin3
  N45: X3.2, Echo_sounder2.pin4
  N46: X3.3, Pressure_sensor2.pin2
  N47: X3.4, Pressure_sensor2.pin1

notes:
  NOTE: Cut the pad between VUSB and VIN on both Teensy 4.0
  Ethernet connection from Switch to Sidescan-sonar and RPi
  USB between teensy ans RPi

custom parts:
  Teensy 4.0: The Teensy is a complete USB-based microcontoller development system, in a very small footprint, capable of implementing many types of projects. All programming is done via the USB port. No special programmer is needed, only a standard micro-USB cable and a PC or Macintosh with a USB port.
  Mini-360 DC-DC Buck converter: Mini-360 DC-DC Buck converter. Tiny buck step down voltage converter, input voltage 4.75 to 23V output 1 to 17V adjustable. Available from ebay and the like.
